# Fritzing sketch schemtic (saved by Fritzing 0.9.5d)
breadboards: 1

parts:
  LCD2 = LCD screen
  LCM1602_IIC2 = LCM1602 IIC [part_number="LCM1602 IIC" chip_label="LCM1602 IIC" package="DIP (Dual Inline) [THT]"]
  U1 = ESP32 [part_number=ESP32]  # not connected
  U1_2 = ESP32 [part_number=ESP32]  # not connected
  U1_3 = ESP32 [part_number=ESP32]  # not connected
  U1_4 = DOIT Esp32 DevKit v1 (30 pins long, 11 pins width) [part_number=ESP32S-PIN30]
  M1 = BMP280

nets:
  VSS: LCD2.VSS, LCM1602_IIC2.VSS
  VDD: LCD2.VDD, LCM1602_IIC2.VDD
  N1: LCD2.V0, LCM1602_IIC2.V0
  N2: LCD2.RS, LCM1602_IIC2.RS
  N3: LCD2.R/W, LCM1602_IIC2.RW
  N4: LCD2.E, LCM1602_IIC2.E
  N5: LCD2.DB0, LCM1602_IIC2.D0
  N6: LCD2.DB1, LCM1602_IIC2.D1
  N7: LCD2.DB2, LCM1602_IIC2.D2
  N8: LCD2.DB3, LCM1602_IIC2.D3
  N9: LCD2.DB4, LCM1602_IIC2.D4
  N10: LCD2.DB5, LCM1602_IIC2.D5
  N11: LCD2.DB6, LCM1602_IIC2.D6
  N12: LCD2.DB7, LCM1602_IIC2.D7
  N13: LCD2.LED+, LCM1602_IIC2.A
  N14: LCD2.LED-, LCM1602_IIC2.K
  GND: LCM1602_IIC2.GND, U1_4.GND, M1.GND
  VCC: LCM1602_IIC2.VCC, U1_4.3V3
  N15: LCM1602_IIC2.SDA, U1_4.D21
  N16: LCM1602_IIC2.SCL, U1_4.D22

custom parts:
  LCM1602 IIC: I2C-Module to use a 1602 or 2004 LCD on with the wire.h libory Serial LCD Modul
  ESP32: Generic WiFi Module based on the ESP32 with onboard PCB antenna and UART communications
  DOIT Esp32 DevKit v1 (30 pins long, 11 pins width): The DOIT Esp32 DevKit v1 is one of the development board created by DOIT to evaluate the ESP-WROOM-32 module. It is based on the ESP32 microcontroller that boasts Wifi, Bluetooth, Ethernet and Low Power support all in a single chip. (vanepp) made breadboard work, adjusted pin numbering and labels and reduced size of schematic and cleaned up pcb. This chip is 30pins long (2 x15) and 11 pins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
  BMP280: Temperature Humidity Barometric presure Sensor, I2C
